# Fritzing sketch pcb (saved by Fritzing 0.9.3b)
circuit board: 15.3953cm x 9.23896cm
breadboards: 1

parts:
  Componente1 = Arduino Mega 2560 (Rev3)
  OMRON3 = Relay [part_number=FRS1B-S package=THT]
  OMRON5 = Relay [part_number=FRS1B-S package=THT]
  OMRON4 = Relay [part_number=FRS1B-S package=THT]
  OMRON2 = Relay [part_number=FRS1B-S package=THT]
  OMRON1 = Relay [part_number=FRS1B-S package=THT]
  OMRON6 = Relay [part_number=FRS1B-S package=THT]
  OMRON7 = Relay [part_number=FRS1B-S package=THT]
  U1_-_https_//www_omron_com/ecb/products/pdf/en-g5q_pdf = RELAY [package=relay-g5q]  # not connected

nets:
  N1: Componente1.D12_PWM, OMRON3.C1
  N2: Componente1.D11_PWM, OMRON5.C1
  N3: Componente1.D10_PWM, OMRON4.C1
  N4: Componente1.D9_PWM, OMRON2.C1
  N5: Componente1.D8_PWM, OMRON1.C1
  N6: Componente1.5V, OMRON3.COIL1, OMRON5.COIL1, OMRON4.COIL1, OMRON2.COIL1, OMRON1.COIL1, OMRON6.COIL1, OMRON7.COIL1
  N7: Componente1.GND, OMRON3.COIL2, OMRON5.COIL2, OMRON4.COIL2, OMRON2.COIL2, OMRON1.COIL2, OMRON6.COIL2, OMRON7.COIL2
  N8: Componente1.D6_PWM, OMRON7.C1
  N9: Componente1.D7_PWM, OMRON6.C1, OMRON6.C2
